// Logisim project NSU-FIT-2021-T04L1e07.circ as structural Verilog: 1 circuit, main circuit mycircuit
module mycircuit (
  input  A,
  input  B,
  input  C,
  output R
);

  wire xnor_1_out, xor_1_out;

  xor xor_1 (xor_1_out, A, B);
  xnor xnor_1 (xnor_1_out, A, C);
  and and_1 (R, xor_1_out, xnor_1_out);
endmodule
