// Logisim project NSU-FIT-2021-T05L2e01.circ as structural Verilog: 1 circuit, main circuit inc
module inc (
  input  [7:0] X,
  output [7:0] R,
  output Cout
);

  wire [6:0] and_1_out;

  assign {Cout, and_1_out} = X & {and_1_out, 1'b1};  // AND_Gate and_1, 8 bits wide
  assign R = X ^ {and_1_out, 1'b1};  // XOR_Gate xor_1, 8 bits wide
endmodule
