// Logisim project NSU-FIT-2021-T05L2e02.circ as structural Verilog: 2 circuits, main circuit dec
module dec (
  input  [7:0] X,
  output [7:0] R,
  output Cout
);

  _1 u_1_1 (.A(X), .Res(R), .Cout(Cout));
endmodule

module _1 (
  input  [7:0] A,
  output [7:0] Res,
  output Cout
);

  wire [7:1] and_1_out;

  assign {Cout, and_1_out} = A & ~{and_1_out, 1'b0};  // AND_Gate and_1, 8 bits wide
  assign Res = A ^ {and_1_out, 1'b0};  // XOR_Gate xor_1, 8 bits wide
endmodule
