// Logisim project NSU-FIT-2021-T05L2e03.circ as structural Verilog: 3 circuits, main circuit formula
module formula (
  input  [7:0] A,
  output [7:0] R,
  output OFL
);

  wire shla_2_cout, shla_cout, sum_1_cout;
  wire [7:0] shla_2_res, shla_res;

  shla shla (.A(A), .Res(shla_res), .Cout(shla_cout));
  shla shla_2 (.A(shla_res), .Res(shla_2_res), .Cout(shla_2_cout));
  sum sum_1 (.A(A), .B(shla_2_res), .sum(R), .Cout(sum_1_cout));
  or or_1 (OFL, shla_cout, shla_2_cout, sum_1_cout);
endmodule

module sum (
  input  [7:0] A,
  input  [7:0] B,
  output [7:0] sum,
  output Cout
);

  wire [6:0] or_1_out;
  wire [7:0] and_1_out, and_2_out, and_3_out;

  assign and_1_out = A & B;  // AND_Gate and_1, 8 bits wide
  assign and_2_out = B & {or_1_out, 1'b0};  // AND_Gate and_2, 8 bits wide
  assign and_3_out = A & {or_1_out, 1'b0};  // AND_Gate and_3, 8 bits wide
  assign {Cout, or_1_out} = and_1_out | and_2_out | and_3_out;  // OR_Gate or_1, 8 bits wide
  assign sum = A ^ {or_1_out, 1'b0} ^ B;  // XOR_Gate xor_1, 8 bits wide
endmodule

module shla (
  input  [7:0] A,
  output [7:0] Res,
  output Cout
);


  assign Cout = A[7];
  assign Res = {A[6:0], 1'b0};
endmodule
