// Logisim project NSU-FIT-2021-T05L2e05.circ as structural Verilog: 3 circuits, main circuit bcd2
module bcd2 (
  input  Cin,
  input  [7:0] A,
  input  [7:0] B,
  output [7:0] R,
  output Cout
);

  wire bcd_add_1_cout;

  Hex_Digit_Display hex_digit_display_1 (.value(A[7:4]));  // open: dp
  Hex_Digit_Display hex_digit_display_2 (.value(B[7:4]));  // open: dp
  Hex_Digit_Display hex_digit_display_3 (.value({3'b000, Cin}));  // open: dp
  Hex_Digit_Display hex_digit_display_4 (.value(A[3:0]));  // open: dp
  Hex_Digit_Display hex_digit_display_5 (.value(B[3:0]));  // open: dp
  bcd_add bcd_add_1 (.Cin(Cin), .A(A[3:0]), .B(B[3:0]), .A_2(R[3:0]), .Cout(bcd_add_1_cout));
  bcd_add bcd_add_2 (.Cin(bcd_add_1_cout), .A(A[7:4]), .B(B[7:4]), .A_2(R[7:4]), .Cout(Cout));
  Hex_Digit_Display hex_digit_display_6 (.value({3'b000, Cout}));  // open: dp
  Hex_Digit_Display hex_digit_display_7 (.value(R[7:4]));  // open: dp
  Hex_Digit_Display hex_digit_display_8 (.value(R[3:0]));  // open: dp
endmodule

// BCD
module bcd_add (
  input  Cin,
  input  [3:0] A,
  input  [3:0] B,
  output [3:0] A_2,
  output Cout
);

  wire and_1_out, n4sum_1_cout, or_1_out;
  wire [3:0] n4sum_1_res;

  _4sum u_4sum_1 (.A(A), .B(B), .Cin(Cin), .Res(n4sum_1_res), .Cout(n4sum_1_cout));
  or or_1 (or_1_out, n4sum_1_res[1], n4sum_1_res[2]);
  and and_1 (and_1_out, or_1_out, n4sum_1_res[3]);
  or or_2 (Cout, and_1_out, n4sum_1_cout);
  _4sum u_4sum_2 (.A({1'b0, {2{Cout}}, 1'b0}), .B(n4sum_1_res), .Cin(1'b0), .Res(A_2));  // open: Cout
endmodule

module _4sum (
  input  [3:0] A,
  input  [3:0] B,
  input  Cin,
  output [3:0] Res,
  output Cout
);

  wire [3:0] and_1_out, and_2_out, and_3_out;
  wire [3:1] or_1_out;

  assign and_1_out = A & B;  // AND_Gate and_1, 4 bits wide
  assign and_2_out = A & {or_1_out, Cin};  // AND_Gate and_2, 4 bits wide
  assign and_3_out = B & {or_1_out, Cin};  // AND_Gate and_3, 4 bits wide
  assign {Cout, or_1_out} = and_1_out | and_2_out | and_3_out;  // OR_Gate or_1, 4 bits wide
  assign Res = A ^ B ^ {or_1_out, Cin};  // XOR_Gate xor_1, 4 bits wide
endmodule
