// Logisim project NSU-FIT-2021-T05L3e02.circ as structural Verilog: 4 circuits, main circuit cmp
module cmp (
  input  [7:0] A,
  input  [7:0] B,
  output Gt,
  output Eq
);

  wire [7:0] and_1_out, gethighest_1_res, xor_1_out;

  assign xor_1_out = A ^ B;  // XOR_Gate xor_1, 8 bits wide
  getHighest gethighest_1 (.X(xor_1_out), .Res(gethighest_1_res));
  assign and_1_out = A & gethighest_1_res;  // AND_Gate and_1, 8 bits wide
  or or_1 (Gt, and_1_out[0], and_1_out[1], and_1_out[2], and_1_out[3], and_1_out[4], and_1_out[5], and_1_out[6], and_1_out[7]);
  nor nor_1 (Eq, xor_1_out[0], xor_1_out[1], xor_1_out[2], xor_1_out[3], xor_1_out[4], xor_1_out[5], xor_1_out[6], xor_1_out[7]);

  // Notes on the sheet:
  //   A: pull=up
endmodule

module getHighest (
  input  [7:0] X,
  output [7:0] Res
);

  wire [7:0] and_1_out, or_1_out;

  assign and_1_out = {1'b1, and_1_out[7:1]} & ~X;  // AND_Gate and_1, 8 bits wide
  assign or_1_out = ~{1'b1, and_1_out[7:1]} | and_1_out;  // OR_Gate or_1, 8 bits wide
  assign Res = ~or_1_out;  // NOT_Gate not_1, 8 bits wide
endmodule

module cmp1 (
  input  [7:0] A,
  input  [7:0] B,
  output [7:0] Res
);

  wire [7:0] not_1_out;

  assign Res = A & not_1_out & ~B;  // AND_Gate and_1, 8 bits wide
  assign not_1_out = ~{1'b0, Res[7:1]};  // NOT_Gate not_1, 8 bits wide

  // Notes on the sheet:
  //   A: pull=up
endmodule

module cmp_2 (
  input  [7:0] A,
  input  [7:0] B
);

  wire [7:0] xor_1_out;

  assign xor_1_out = A ^ B;  // XOR_Gate xor_1, 8 bits wide

  // Notes on the sheet:
  //   A: pull=up
endmodule
